// Logisim project LAB2_202173628-K_202173651-4.circ as structural Verilog: 11 circuits, main circuit main
module main (
  input  [2:0] Eje_X,
  input  [2:0] Eje_Y,
  output [2:0] Eje_X_2,
  output [2:0] Eje_Y_2,
  output [3:0] Direccion
);

  wire clock_1_out, clock_2_out;
  wire [2:0] d_ffs_1_out_5, d_ffs_1_out_6, multiplexer_1_out, multiplexer_2_out;
  wire [3:0] \circuito_1_1_dirección ;

  Multiplexer #(.width(3)) multiplexer_1 (
    .in0(Eje_X), .in1(Eje_X_2), .out(multiplexer_1_out), .sel(clock_1_out));  // open: en
  Multiplexer #(.width(3)) multiplexer_2 (
    .in0(Eje_Y), .in1(Eje_Y_2), .out(multiplexer_2_out), .sel(clock_1_out));  // open: en
  Clock #(.highDuration(28), .lowDuration(2)) clock_1 (.out(clock_1_out));
  Circuito_1 circuito_1_1 (.X(multiplexer_1_out), .Y(multiplexer_2_out), .\Dirección (\circuito_1_1_dirección ));
  Clock clock_2 (.out(clock_2_out));
  D_Flip_Flops d_ffs_1 (
    .in_2(multiplexer_1_out), .in_3(multiplexer_2_out), .in_4(\circuito_1_1_dirección ),
    .out_5(d_ffs_1_out_5), .out_6(d_ffs_1_out_6), .out_7(Direccion), .in_1(clock_2_out));
  Circuito_2 circuito_2_1 (.X(d_ffs_1_out_5), .Y(d_ffs_1_out_6), .Direccion(Direccion), .X_2(Eje_X_2), .Y_2(Eje_Y_2));
endmodule

module Circuito_1 (
  input  [2:0] X,
  input  [2:0] Y,
  output [3:0] \Dirección 
);

  wire and_1_out, and_2_out, and_3_out, and_4_out, and_5_out, and_6_out, and_7_out, and_8_out, and_9_out,
       and_10_out, and_11_out, and_12_out, and_13_out, and_14_out, and_15_out, and_16_out, and_17_out,
       and_18_out, and_19_out, and_20_out, and_21_out, and_22_out, and_23_out, and_24_out, and_25_out,
       not_1_out, not_2_out, not_3_out, not_4_out, not_5_out, not_6_out, not_7_out, not_8_out, not_9_out,
       not_10_out, not_11_out, not_12_out, not_13_out, not_14_out, not_15_out, not_16_out, not_17_out,
       not_18_out, not_19_out, not_20_out, not_21_out, not_22_out, not_23_out, not_24_out, not_25_out,
       not_26_out, not_27_out, not_28_out, not_29_out, not_30_out, not_31_out, not_32_out, not_33_out,
       not_34_out, not_35_out, not_36_out, not_37_out, not_38_out, not_39_out, not_40_out, not_41_out,
       not_42_out, not_43_out, not_44_out, not_45_out, not_46_out, not_47_out, not_48_out, not_49_out,
       not_50_out, not_51_out, not_52_out, not_53_out, not_54_out, not_55_out, not_56_out, not_57_out,
       not_58_out, not_59_out, not_60_out, not_61_out, not_62_out, not_63_out, not_64_out, not_65_out,
       not_66_out, not_67_out, not_68_out, not_69_out, not_70_out, not_71_out, not_72_out, not_73_out,
       not_74_out;

  not not_1 (not_1_out, X[2]);
  not not_2 (not_2_out, X[1]);
  not not_3 (not_3_out, X[0]);
  not not_4 (not_4_out, Y[2]);
  not not_5 (not_5_out, Y[1]);
  not not_6 (not_6_out, Y[0]);
  not not_7 (not_7_out, X[1]);
  not not_8 (not_8_out, X[0]);
  not not_9 (not_9_out, Y[2]);
  not not_10 (not_10_out, Y[1]);
  not not_11 (not_11_out, Y[0]);
  not not_12 (not_12_out, X[2]);
  not not_13 (not_13_out, X[1]);
  not not_14 (not_14_out, X[0]);
  not not_15 (not_15_out, Y[2]);
  not not_16 (not_16_out, Y[1]);
  not not_17 (not_17_out, Y[0]);
  not not_18 (not_18_out, X[2]);
  not not_19 (not_19_out, X[1]);
  not not_20 (not_20_out, Y[2]);
  not not_21 (not_21_out, Y[0]);
  not not_22 (not_22_out, Y[1]);
  not not_23 (not_23_out, Y[0]);
  not not_24 (not_24_out, X[2]);
  not not_25 (not_25_out, X[1]);
  not not_26 (not_26_out, X[0]);
  not not_27 (not_27_out, Y[2]);
  not not_28 (not_28_out, Y[1]);
  not not_29 (not_29_out, Y[0]);
  not not_30 (not_30_out, X[2]);
  not not_31 (not_31_out, Y[2]);
  not not_32 (not_32_out, X[1]);
  not not_33 (not_33_out, X[0]);
  not not_34 (not_34_out, Y[2]);
  not not_35 (not_35_out, Y[1]);
  not not_36 (not_36_out, X[1]);
  not not_37 (not_37_out, X[0]);
  not not_38 (not_38_out, Y[2]);
  not not_39 (not_39_out, Y[0]);
  not not_40 (not_40_out, X[1]);
  not not_41 (not_41_out, X[0]);
  not not_42 (not_42_out, Y[1]);
  not not_43 (not_43_out, Y[0]);
  not not_44 (not_44_out, X[2]);
  not not_45 (not_45_out, X[1]);
  not not_46 (not_46_out, X[0]);
  not not_47 (not_47_out, Y[2]);
  not not_48 (not_48_out, Y[1]);
  not not_49 (not_49_out, Y[0]);
  not not_50 (not_50_out, X[2]);
  not not_51 (not_51_out, X[1]);
  not not_52 (not_52_out, Y[2]);
  not not_53 (not_53_out, Y[0]);
  not not_54 (not_54_out, Y[2]);
  not not_55 (not_55_out, Y[0]);
  not not_56 (not_56_out, X[2]);
  not not_57 (not_57_out, X[0]);
  not not_58 (not_58_out, X[0]);
  not not_59 (not_59_out, Y[1]);
  not not_60 (not_60_out, X[1]);
  not not_61 (not_61_out, X[0]);
  not not_62 (not_62_out, Y[0]);
  not not_63 (not_63_out, X[2]);
  not not_64 (not_64_out, Y[2]);
  not not_65 (not_65_out, Y[1]);
  not not_66 (not_66_out, X[2]);
  not not_67 (not_67_out, Y[2]);
  not not_68 (not_68_out, Y[1]);
  not not_69 (not_69_out, X[2]);
  not not_70 (not_70_out, Y[0]);
  not not_71 (not_71_out, Y[1]);
  not not_72 (not_72_out, Y[0]);
  not not_73 (not_73_out, X[1]);
  not not_74 (not_74_out, Y[1]);
  and and_1 (and_1_out, not_1_out, not_2_out, not_3_out, not_4_out, not_5_out, not_6_out);
  and and_2 (and_2_out, X[2], not_7_out, not_8_out, not_9_out, Y[1], Y[0]);
  and and_3 (and_3_out, X[2], X[0], not_52_out, Y[1], not_53_out);
  and and_4 (and_4_out, X[2], X[0], Y[2], Y[1], Y[0]);
  and and_5 (and_5_out, X[2], X[1], not_54_out, Y[1], not_55_out);
  and and_6 (and_6_out, X[2], X[1], X[0], Y[2], not_10_out, not_11_out);
  and and_7 (and_7_out, not_12_out, not_13_out, not_14_out, not_15_out, not_16_out, not_17_out);
  and and_8 (and_8_out, not_18_out, not_19_out, X[0], not_20_out, Y[1], not_21_out);
  and and_9 (and_9_out, not_56_out, X[1], not_57_out, Y[2], Y[0]);
  and and_10 (and_10_out, X[1], not_58_out, Y[2], not_59_out, Y[0]);
  and and_11 (and_11_out, X[2], not_60_out, not_61_out, Y[2], Y[1]);
  and and_12 (and_12_out, X[2], X[1], X[0], Y[2], not_22_out, not_23_out);
  and and_13 (and_13_out, not_24_out, not_25_out, not_26_out, not_27_out, not_28_out, not_29_out);
  and and_14 (and_14_out, not_30_out, X[1], X[0], not_31_out, Y[1], Y[0]);
  and and_15 (and_15_out, X[2], not_32_out, not_33_out, not_34_out, not_35_out, Y[0]);
  and and_16 (and_16_out, X[2], not_36_out, not_37_out, not_38_out, Y[1], not_39_out);
  and and_17 (and_17_out, X[2], not_40_out, not_41_out, Y[2], not_42_out, not_43_out);
  and and_18 (and_18_out, X[2], X[1], X[0], Y[2], not_62_out);
  and and_19 (and_19_out, not_44_out, not_45_out, not_46_out, not_47_out, not_48_out, not_49_out);
  and and_20 (and_20_out, not_63_out, X[0], not_64_out, not_65_out, Y[0]);
  and and_21 (and_21_out, not_50_out, not_51_out, X[0], Y[2], Y[1], Y[0]);
  and and_22 (and_22_out, not_66_out, X[1], not_67_out, not_68_out, Y[0]);
  and and_23 (and_23_out, not_69_out, X[1], Y[2], not_70_out);
  and and_24 (and_24_out, X[1], Y[2], not_71_out, not_72_out);
  and and_25 (and_25_out, X[2], not_73_out, Y[2], not_74_out, Y[0]);
  or or_1 (\Dirección [3], and_1_out, and_2_out, and_3_out, and_4_out, and_5_out, and_6_out);
  or or_2 (\Dirección [2], and_7_out, and_8_out, and_9_out, and_10_out, and_11_out, and_12_out);
  or or_3 (\Dirección [1], and_13_out, and_14_out, and_15_out, and_16_out, and_17_out, and_18_out);
  or or_4 (\Dirección [0], and_19_out, and_20_out, and_21_out, and_22_out, and_23_out, and_24_out, and_25_out);
endmodule

module Circuito_2 (
  input  [2:0] X,
  input  [2:0] Y,
  input  [3:0] Direccion,
  output [2:0] X_2,
  output [2:0] Y_2
);

  wire and_1_out, and_2_out, and_3_out, and_4_out, and_5_out, and_6_out, and_7_out, and_8_out, and_9_out,
       and_10_out, and_11_out, and_12_out, and_13_out, and_14_out, and_15_out, and_16_out, and_17_out,
       and_18_out, and_19_out, and_20_out, and_21_out, and_22_out, and_23_out, not_1_out, not_2_out,
       not_3_out, not_4_out, not_5_out, not_6_out, not_7_out, not_8_out, not_9_out, not_10_out, not_11_out,
       not_12_out, not_13_out, not_14_out, not_15_out, not_16_out, not_17_out, not_18_out, not_19_out,
       not_20_out, not_21_out, not_22_out, not_23_out, not_24_out, not_25_out, not_26_out, not_27_out,
       not_28_out;

  not not_1 (not_1_out, X[0]);
  not not_2 (not_2_out, Direccion[3]);
  not not_3 (not_3_out, Y[0]);
  not not_4 (not_4_out, X[0]);
  not not_5 (not_5_out, X[1]);
  not not_6 (not_6_out, X[0]);
  not not_7 (not_7_out, Direccion[3]);
  not not_8 (not_8_out, Direccion[0]);
  not not_9 (not_9_out, X[2]);
  not not_10 (not_10_out, X[1]);
  not not_11 (not_11_out, Y[2]);
  not not_12 (not_12_out, X[0]);
  not not_13 (not_13_out, Direccion[2]);
  not not_14 (not_14_out, Direccion[1]);
  not not_15 (not_15_out, X[2]);
  not not_16 (not_16_out, X[0]);
  not not_17 (not_17_out, Y[0]);
  not not_18 (not_18_out, Direccion[2]);
  not not_19 (not_19_out, Direccion[2]);
  not not_20 (not_20_out, Direccion[1]);
  not not_21 (not_21_out, Direccion[1]);
  not not_22 (not_22_out, Y[2]);
  not not_23 (not_23_out, X[1]);
  not not_24 (not_24_out, Y[0]);
  not not_25 (not_25_out, Direccion[3]);
  not not_26 (not_26_out, Y[0]);
  not not_27 (not_27_out, Direccion[2]);
  not not_28 (not_28_out, Direccion[1]);
  and and_1 (and_1_out, X[1], X[0], Direccion[0]);
  and and_2 (and_2_out, X[2], not_1_out, not_2_out);
  and and_3 (and_3_out, X[2], Y[1], not_3_out);
  and and_4 (and_4_out, X[2], X[0], Y[0]);
  and and_5 (and_5_out, not_4_out, Y[0], Direccion[3]);
  and and_6 (and_6_out, not_5_out, X[0], Direccion[0]);
  and and_7 (and_7_out, X[0], Direccion[1]);
  and and_8 (and_8_out, X[1], not_6_out, not_7_out);
  and and_9 (and_9_out, X[1], X[0], Y[1], not_8_out);
  and and_10 (and_10_out, not_9_out, not_10_out, not_11_out);
  and and_11 (and_11_out, not_12_out, not_13_out, not_14_out);
  and and_12 (and_12_out, X[0], Direccion[1]);
  and and_13 (and_13_out, not_15_out, Direccion[1]);
  and and_14 (and_14_out, not_16_out, Y[2]);
  and and_15 (and_15_out, Y[2], Direccion[0]);
  and and_16 (and_16_out, Y[2], Y[1]);
  and and_17 (and_17_out, Y[1], not_17_out, not_18_out);
  and and_18 (and_18_out, Y[1], not_19_out, not_20_out);
  and and_19 (and_19_out, Y[1], Y[0], not_21_out);
  and and_20 (and_20_out, X[2], not_22_out);
  and and_21 (and_21_out, not_23_out, not_24_out, not_25_out);
  and and_22 (and_22_out, not_26_out, Direccion[1]);
  and and_23 (and_23_out, Y[0], not_27_out, not_28_out);
  or or_1 (X_2[2], and_1_out, and_2_out, and_3_out, and_4_out);
  or or_2 (X_2[1], and_5_out, and_6_out, and_7_out, and_8_out, and_9_out);
  or or_3 (X_2[0], and_10_out, and_11_out, and_12_out);
  or or_4 (Y_2[2], and_13_out, and_14_out, and_15_out, and_16_out);
  or or_5 (Y_2[1], and_17_out, and_18_out, and_19_out, and_20_out);
  or or_6 (Y_2[0], and_21_out, and_22_out, and_23_out);
endmodule

module SR_Latch (
  input  in_1,
  input  in_2,
  output out_3,
  output out_4
);

  wire or_1_out, or_2_out;

  or or_1 (or_1_out, in_1, out_4);
  or or_2 (or_2_out, out_3, in_2);
  not not_1 (out_3, or_1_out);
  not not_2 (out_4, or_2_out);
endmodule

module D_Latch (
  input  in_1,
  input  in_2,
  output out_3,
  output out_4
);

  wire and_1_out, and_2_out, not_1_out;

  not not_1 (not_1_out, in_2);
  and and_1 (and_1_out, in_1, not_1_out);
  and and_2 (and_2_out, in_1, in_2);
  SR_Latch sr_latch_1 (.in_1(and_1_out), .in_2(and_2_out), .out_3(out_3), .out_4(out_4));
endmodule

module D_Flip_Flop (
  input  in_1,
  input  in_2,
  output out_3
);

  wire d_latch_1_out_3, not_1_out;

  not not_1 (not_1_out, in_1);
  D_Latch d_latch_1 (.in_1(not_1_out), .in_2(in_2), .out_3(d_latch_1_out_3));  // open: out_4
  D_Latch d_latch_2 (.in_1(in_1), .in_2(d_latch_1_out_3), .out_3(out_3));  // open: out_4
endmodule

module _3_D_Flip_Flop (
  input  in_1,
  input  [2:0] in_2,
  output [2:0] out_3
);

  D_Flip_Flop d_ff_1 (.in_2(in_2[0]), .out_3(out_3[0]), .in_1(in_1));
  D_Flip_Flop d_ff_2 (.in_2(in_2[1]), .out_3(out_3[1]), .in_1(in_1));
  D_Flip_Flop d_ff_3 (.in_2(in_2[2]), .out_3(out_3[2]), .in_1(in_1));
endmodule

module _4FF (
  input  in_1,
  input  [3:0] in_2,
  output [3:0] out_3
);

  _3_D_Flip_Flop u_3_d_ff_1 (.in_2(in_2[2:0]), .out_3(out_3[2:0]), .in_1(in_1));
  D_Flip_Flop d_ff_1 (.in_2(in_2[3]), .out_3(out_3[3]), .in_1(in_1));
endmodule

module D_Flip_Flops (
  input  in_1,
  input  [2:0] in_2,
  input  [2:0] in_3,
  input  [3:0] in_4,
  output [2:0] out_5,
  output [2:0] out_6,
  output [3:0] out_7
);

  _3_D_Flip_Flop u_3_d_ff_1 (.in_2(in_2), .out_3(out_5), .in_1(in_1));
  _3_D_Flip_Flop u_3_d_ff_2 (.in_2(in_3), .out_3(out_6), .in_1(in_1));
  _4FF u_4ff_1 (.in_1(in_1), .in_2(in_4), .out_3(out_7));
endmodule

module Nuevo_estado (
  input  [2:0] in_1,
  input  [2:0] in_2,
  output [2:0] out_3,
  output [2:0] out_4,
  output [3:0] out_5
);

  Circuito_1 circuito_1_1 (.X(in_1), .Y(in_2), .\Dirección (out_5));
  Circuito_2 circuito_2_1 (.X(in_1), .Y(in_2), .Direccion(out_5), .X_2(out_3), .Y_2(out_4));
endmodule

module N (
  input  [2:0] Eje_X,
  input  [2:0] Eje_Y,
  output [2:0] Eje_X_2,
  output [2:0] Eje_Y_2,
  output [3:0] Direccion
);

  wire clock_1_out, clock_2_out;
  wire [2:0] multiplexer_1_out, multiplexer_2_out;

  Multiplexer #(.width(3)) multiplexer_1 (
    .in0(Eje_X), .in1(Eje_X_2), .out(multiplexer_1_out), .sel(clock_1_out));  // open: en
  Multiplexer #(.width(3)) multiplexer_2 (
    .in0(Eje_Y), .in1(Eje_Y_2), .out(multiplexer_2_out), .sel(clock_1_out));  // open: en
  Clock #(.highDuration(28), .lowDuration(2)) clock_1 (.out(clock_1_out));
  Clock clock_2 (.out(clock_2_out));
  D_Flip_Flops d_ffs_1 (.in_1(clock_2_out));  // open: in_2, in_3, in_4, out_5, out_6, out_7
endmodule
